// Logisim project Projeto - Sistemas Digitais.circ as structural Verilog: 4 circuits, main circuit main
module main (
  input  A,
  input  B,
  input  C,
  input  D,
  input  A_2,
  input  A_3,
  input  B_2,
  input  B_3,
  input  C_2,
  input  C_3,
  input  D_2,
  input  D_3,
  input  W,
  input  X,
  input  Y,
  input  Z,
  output W_2,
  output X_2,
  output Y_2,
  output Z_2
);

  wire codificador_bcd_pra_gray_2_w, codificador_bcd_pra_gray_2_x, codificador_bcd_pra_gray_2_y,
       codificador_bcd_pra_gray_2_z, decodificador_bcd_para_7_segmentos_1_a_2,
       decodificador_bcd_para_7_segmentos_1_b_2, decodificador_bcd_para_7_segmentos_1_c_2,
       decodificador_bcd_para_7_segmentos_1_d_2, decodificador_bcd_para_7_segmentos_1_e,
       decodificador_bcd_para_7_segmentos_1_f, decodificador_bcd_para_7_segmentos_1_g,
       decodificador_gray_pra_7_segmentos_1_a, decodificador_gray_pra_7_segmentos_1_b,
       decodificador_gray_pra_7_segmentos_1_c, decodificador_gray_pra_7_segmentos_1_d,
       decodificador_gray_pra_7_segmentos_1_e, decodificador_gray_pra_7_segmentos_1_f,
       decodificador_gray_pra_7_segmentos_1_g, decodificador_gray_pra_7_segmentos_2_a,
       decodificador_gray_pra_7_segmentos_2_b, decodificador_gray_pra_7_segmentos_2_c,
       decodificador_gray_pra_7_segmentos_2_d, decodificador_gray_pra_7_segmentos_2_e,
       decodificador_gray_pra_7_segmentos_2_f, decodificador_gray_pra_7_segmentos_2_g;

  Codificador___BCD_pra_Gray codificador_bcd_pra_gray_1 (
    .A(A), .B(B), .C(C), .D(D), .W(W_2), .X(X_2), .Y(Y_2), .Z(Z_2));
  Decodificador___BCD_para_7_Segmentos decodificador_bcd_para_7_segmentos_1 (
    .A(A_3), .B(B_3), .C(C_3), .D(D_3), .a_2(decodificador_bcd_para_7_segmentos_1_a_2),
    .b_2(decodificador_bcd_para_7_segmentos_1_b_2), .c_2(decodificador_bcd_para_7_segmentos_1_c_2),
    .d_2(decodificador_bcd_para_7_segmentos_1_d_2), .e(decodificador_bcd_para_7_segmentos_1_e),
    .f(decodificador_bcd_para_7_segmentos_1_f), .g(decodificador_bcd_para_7_segmentos_1_g));
  Decodificador___Gray_pra_7_Segmentos decodificador_gray_pra_7_segmentos_1 (
    .W(W), .X(X), .Y(Y), .Z(Z), .a(decodificador_gray_pra_7_segmentos_1_a),
    .b(decodificador_gray_pra_7_segmentos_1_b), .c(decodificador_gray_pra_7_segmentos_1_c),
    .d(decodificador_gray_pra_7_segmentos_1_d), .e(decodificador_gray_pra_7_segmentos_1_e),
    .f(decodificador_gray_pra_7_segmentos_1_f), .g(decodificador_gray_pra_7_segmentos_1_g));
  _7_Segment_Display u_7_segment_display_1 (
    .g(decodificador_bcd_para_7_segmentos_1_g), .f(decodificador_bcd_para_7_segmentos_1_f),
    .a(decodificador_bcd_para_7_segmentos_1_a_2), .b(decodificador_bcd_para_7_segmentos_1_b_2),
    .e(decodificador_bcd_para_7_segmentos_1_e), .d(decodificador_bcd_para_7_segmentos_1_d_2),
    .c(decodificador_bcd_para_7_segmentos_1_c_2));  // open: dp
  _7_Segment_Display u_7_segment_display_2 (
    .g(decodificador_gray_pra_7_segmentos_1_g), .f(decodificador_gray_pra_7_segmentos_1_f),
    .a(decodificador_gray_pra_7_segmentos_1_a), .b(decodificador_gray_pra_7_segmentos_1_b),
    .e(decodificador_gray_pra_7_segmentos_1_e), .d(decodificador_gray_pra_7_segmentos_1_d),
    .c(decodificador_gray_pra_7_segmentos_1_c));  // open: dp
  Codificador___BCD_pra_Gray codificador_bcd_pra_gray_2 (
    .A(A_2), .B(B_2), .C(C_2), .D(D_2), .W(codificador_bcd_pra_gray_2_w), .X(codificador_bcd_pra_gray_2_x),
    .Y(codificador_bcd_pra_gray_2_y), .Z(codificador_bcd_pra_gray_2_z));
  Decodificador___Gray_pra_7_Segmentos decodificador_gray_pra_7_segmentos_2 (
    .W(codificador_bcd_pra_gray_2_w), .X(codificador_bcd_pra_gray_2_x), .Y(codificador_bcd_pra_gray_2_y),
    .Z(codificador_bcd_pra_gray_2_z), .a(decodificador_gray_pra_7_segmentos_2_a),
    .b(decodificador_gray_pra_7_segmentos_2_b), .c(decodificador_gray_pra_7_segmentos_2_c),
    .d(decodificador_gray_pra_7_segmentos_2_d), .e(decodificador_gray_pra_7_segmentos_2_e),
    .f(decodificador_gray_pra_7_segmentos_2_f), .g(decodificador_gray_pra_7_segmentos_2_g));
  _7_Segment_Display u_7_segment_display_3 (
    .g(decodificador_gray_pra_7_segmentos_2_g), .f(decodificador_gray_pra_7_segmentos_2_f),
    .a(decodificador_gray_pra_7_segmentos_2_a), .b(decodificador_gray_pra_7_segmentos_2_b),
    .e(decodificador_gray_pra_7_segmentos_2_e), .d(decodificador_gray_pra_7_segmentos_2_d),
    .c(decodificador_gray_pra_7_segmentos_2_c));  // open: dp
endmodule

module Codificador___BCD_pra_Gray (
  input  A,
  input  B,
  input  C,
  input  D,
  output W,
  output X,
  output Y,
  output Z
);

  wire and_1_out, and_2_out, and_3_out, and_4_out, and_5_out, and_6_out, not_1_out, not_2_out, not_3_out,
       not_4_out, not_5_out, not_6_out;

  not not_1 (not_1_out, A);
  and and_1 (and_1_out, not_1_out, B);
  and and_2 (and_2_out, A, not_2_out);
  not not_2 (not_2_out, B);
  not not_3 (not_3_out, B);
  and and_3 (and_3_out, not_3_out, C);
  and and_4 (and_4_out, B, not_4_out);
  not not_4 (not_4_out, C);
  not not_5 (not_5_out, C);
  and and_5 (and_5_out, not_5_out, D);
  and and_6 (and_6_out, C, not_6_out);
  not not_6 (not_6_out, D);
  or or_1 (X, and_1_out, and_2_out);
  or or_2 (Y, and_3_out, and_4_out);
  or or_3 (Z, and_5_out, and_6_out);

  assign W = A;
endmodule

module Decodificador___BCD_para_7_Segmentos (
  input  A,
  input  B,
  input  C,
  input  D,
  output a_2,
  output b_2,
  output c_2,
  output d_2,
  output e,
  output f,
  output g
);

  wire and_1_out, and_2_out, and_3_out, and_4_out, and_5_out, and_6_out, and_7_out, and_8_out, and_9_out,
       and_10_out, and_11_out, and_12_out, and_13_out, and_14_out, and_15_out, and_16_out, and_17_out,
       and_18_out, and_19_out, and_20_out, and_21_out, and_22_out, and_23_out, and_24_out, and_25_out,
       not_1_out, not_2_out, not_3_out, not_4_out, not_5_out, not_6_out, not_7_out, not_8_out, not_9_out,
       not_10_out, not_11_out, not_12_out, not_13_out, not_14_out, not_15_out, not_16_out, not_17_out,
       not_18_out, not_19_out, not_20_out, not_21_out, not_22_out, not_23_out, not_24_out, not_25_out,
       not_26_out, not_27_out, not_28_out, not_29_out;

  not not_1 (not_1_out, C);
  and and_1 (and_1_out, not_1_out, D);
  not not_2 (not_2_out, A);
  and and_2 (and_2_out, not_2_out, B, not_3_out);
  not not_3 (not_3_out, D);
  and and_3 (and_3_out, A, not_4_out);
  not not_4 (not_4_out, B);
  and and_4 (and_4_out, A, C);
  not not_5 (not_5_out, A);
  and and_5 (and_5_out, not_5_out, not_6_out);
  not not_6 (not_6_out, B);
  not not_7 (not_7_out, B);
  and and_6 (and_6_out, not_7_out, not_8_out);
  not not_8 (not_8_out, D);
  and and_7 (and_7_out, C, D);
  and and_8 (and_8_out, A, C);
  and and_9 (and_9_out, A, B, D);
  not not_9 (not_9_out, A);
  and and_10 (and_10_out, not_9_out, not_10_out);
  not not_10 (not_10_out, B);
  not not_11 (not_11_out, B);
  and and_11 (and_11_out, not_11_out, not_12_out);
  not not_12 (not_12_out, D);
  not not_13 (not_13_out, C);
  and and_12 (and_12_out, not_13_out, not_14_out);
  not not_14 (not_14_out, D);
  and and_13 (and_13_out, C, D);
  not not_15 (not_15_out, A);
  and and_14 (and_14_out, not_15_out, B, not_16_out);
  not not_16 (not_16_out, D);
  not not_17 (not_17_out, B);
  and and_15 (and_15_out, A, not_17_out, not_18_out);
  not not_18 (not_18_out, C);
  not not_19 (not_19_out, C);
  and and_16 (and_16_out, A, B);
  not not_20 (not_20_out, A);
  and and_17 (and_17_out, not_20_out, not_21_out);
  not not_21 (not_21_out, C);
  not not_22 (not_22_out, B);
  and and_18 (and_18_out, not_22_out, D);
  and and_19 (and_19_out, B, not_23_out);
  not not_23 (not_23_out, D);
  and and_20 (and_20_out, A, B);
  not not_24 (not_24_out, A);
  not not_25 (not_25_out, A);
  not not_26 (not_26_out, D);
  not not_27 (not_27_out, B);
  not not_28 (not_28_out, C);
  not not_29 (not_29_out, D);
  or or_1 (a_2, and_1_out, and_2_out, and_3_out, and_4_out);
  or or_2 (b_2, and_5_out, and_6_out, and_7_out, and_8_out, and_9_out);
  or or_3 (c_2, and_10_out, and_11_out, C);
  or or_4 (d_2, and_12_out, and_13_out, and_14_out, and_15_out);
  or or_5 (e, not_19_out, D, and_16_out);
  or or_6 (f, and_17_out, and_18_out, and_19_out, and_20_out);
  and and_21 (and_21_out, not_24_out, C, D);
  and and_22 (and_22_out, not_25_out, B, not_26_out);
  and and_23 (and_23_out, B, C);
  and and_24 (and_24_out, A, not_27_out, not_28_out, not_29_out);
  and and_25 (and_25_out, A, B, D);
  or or_7 (g, and_21_out, and_22_out, and_23_out, and_24_out, and_25_out);
endmodule

module Decodificador___Gray_pra_7_Segmentos (
  input  W,
  input  X,
  input  Y,
  input  Z,
  output a,
  output b,
  output c,
  output d,
  output e,
  output f,
  output g
);

  wire and_1_out, and_2_out, and_3_out, and_4_out, and_5_out, and_6_out, and_7_out, and_8_out, and_9_out,
       and_10_out, and_11_out, and_12_out, and_13_out, and_14_out, and_15_out, and_16_out, and_17_out,
       and_18_out, and_19_out, and_20_out, and_21_out, and_22_out, and_23_out, and_24_out, and_25_out,
       and_26_out, and_27_out, not_1_out, not_2_out, not_3_out, not_4_out, not_5_out, not_6_out, not_7_out,
       not_8_out, not_9_out, not_10_out, not_11_out, not_12_out, not_13_out, not_14_out, not_15_out,
       not_16_out, not_17_out, not_18_out, not_19_out, not_20_out, not_21_out, not_22_out, not_23_out,
       not_24_out, not_25_out, not_26_out, not_27_out, not_28_out, not_29_out, not_30_out, not_31_out,
       not_32_out, not_33_out, not_34_out, not_35_out, not_36_out;

  not not_1 (not_1_out, Y);
  and and_1 (and_1_out, not_1_out, Z);
  and and_2 (and_2_out, X, Y);
  and and_3 (and_3_out, W, not_2_out);
  not not_2 (not_2_out, Y);
  and and_4 (and_4_out, W, Z);
  not not_3 (not_3_out, W);
  and and_5 (and_5_out, not_3_out, not_4_out);
  not not_4 (not_4_out, X);
  not not_5 (not_5_out, Y);
  and and_6 (and_6_out, not_5_out, not_6_out);
  not not_6 (not_6_out, Z);
  not not_7 (not_7_out, X);
  and and_7 (and_7_out, not_7_out, Z);
  and and_8 (and_8_out, W, X, Y);
  not not_8 (not_8_out, W);
  and and_9 (and_9_out, not_8_out, not_9_out);
  not not_9 (not_9_out, X);
  not not_10 (not_10_out, W);
  and and_10 (and_10_out, not_10_out, not_11_out);
  not not_11 (not_11_out, Y);
  not not_12 (not_12_out, X);
  and and_11 (and_11_out, not_12_out, not_13_out);
  not not_13 (not_13_out, Y);
  not not_14 (not_14_out, Y);
  and and_12 (and_12_out, not_14_out, not_15_out);
  not not_15 (not_15_out, Z);
  and and_13 (and_13_out, W, X, Y);
  not not_16 (not_16_out, Z);
  and and_14 (and_14_out, X, not_17_out);
  not not_17 (not_17_out, Y);
  not not_18 (not_18_out, X);
  and and_15 (and_15_out, not_18_out, not_19_out);
  not not_19 (not_19_out, Y);
  not not_20 (not_20_out, Z);
  not not_21 (not_21_out, W);
  and and_16 (and_16_out, not_21_out, X, Y);
  and and_17 (and_17_out, W, not_22_out);
  not not_22 (not_22_out, X);
  and and_18 (and_18_out, W, not_23_out);
  not not_23 (not_23_out, Y);
  not not_24 (not_24_out, X);
  and and_19 (and_19_out, not_24_out, not_25_out);
  not not_25 (not_25_out, Y);
  not not_26 (not_26_out, Y);
  and and_20 (and_20_out, not_26_out, Z);
  and and_21 (and_21_out, Y, not_27_out);
  not not_27 (not_27_out, Z);
  not not_28 (not_28_out, W);
  and and_22 (and_22_out, not_28_out, X, Y);
  and and_23 (and_23_out, W, not_29_out);
  not not_29 (not_29_out, X);
  not not_30 (not_30_out, W);
  and and_24 (and_24_out, not_30_out, Y, not_31_out);
  not not_31 (not_31_out, Z);
  not not_32 (not_32_out, W);
  and and_25 (and_25_out, not_32_out, X, not_33_out);
  not not_33 (not_33_out, Y);
  not not_34 (not_34_out, Y);
  and and_26 (and_26_out, W, not_34_out, not_35_out);
  not not_35 (not_35_out, Z);
  and and_27 (and_27_out, W, not_36_out, Z);
  not not_36 (not_36_out, X);
  or or_1 (a, and_1_out, and_2_out, and_3_out, and_4_out);
  or or_2 (b, and_5_out, and_6_out, and_7_out, and_8_out);
  or or_3 (c, and_9_out, and_10_out, and_11_out, and_12_out, and_13_out);
  or or_4 (d, not_16_out, and_14_out);
  or or_5 (e, and_15_out, not_20_out, and_16_out, and_17_out, and_18_out);
  or or_6 (f, and_19_out, and_20_out, and_21_out, and_22_out, and_23_out);
  or or_7 (g, and_24_out, and_25_out, and_26_out, and_27_out);
endmodule
